# Fritzing sketch schematics (saved by Fritzing 0.9.3b)
breadboards: 1

parts:
  WeMos_D1_Mini1 = WeMos D1 Mini  # not connected
  LED1 = LED - 5mm [color="Green (555nm)" package="5 mm [THT]"]
  LED2 = LED - 5mm [color="Yellow (595nm)" package="5 mm [THT]"]
  R1 = Resistor [tolerance=±5% resistance=470 package=THT]
  Part1 = JeePlug experimenter's board
  X1 = DB9 Connector [package=db9]
  U1 = RS232 Transceiver [package=so016]

nets:
  N1: LED1.cathode, LED2.cathode, R1.Pin_1
  N2: R1.Pin_0, Part1.A2
  N3: Part1.B6, X1.5
  N4: Part1.B5, X1.6
  N5: Part1.B4, X1.7
  N6: Part1.B3, X1.8
  N7: Part1.B2, X1.9
  N8: Part1.N$10, U1.V+
  N9: Part1.N$11, U1.C1-
  N10: Part1.N$12, U1.C2+
  N11: Part1.N$13, U1.C2-
  N12: Part1.N$14, U1.V-
  N13: Part1.N$15, U1.T2OUT
  N14: Part1.N$47, U1.VCC
  N15: Part1.N$48, U1.GND
  N16: Part1.N$49, U1.T1OUT
  N17: Part1.N$50, U1.R1IN
  N18: Part1.N$51, U1.R1OUT
  N19: Part1.N$52, U1.T1IN
  N20: Part1.N$53, U1.R2OUT
  N21: Part1.N$54, U1.T2IN
  N22: Part1.N$55, U1.C1+
  N23: Part1.N$57, U1.R2IN

notes:
  VCC
  RXD
  TXD
  GND
  AP
  Station
